# Fritzing sketch 1차시 정선웅 2 (saved by Fritzing 0.8.7b)
breadboards: 1

parts:
  부품1 = Arduino Uno (Rev3)
  R1 = Resistor [tolerance=±5% resistance=33 package=THT]
  LED2 = LED - 5mm [color="Red (633nm)" package="5 mm [THT]"]
  R2 = Resistor [tolerance=±5% resistance=330 package=THT]
  R3 = Resistor [tolerance=±5% resistance=330 package=THT]
  LED4 = LED - 5mm [color="Red (633nm)" package="5 mm [THT]"]
  LED5 = LED - 5mm [color="Red (633nm)" package="5 mm [THT]"]

nets:
  N1: 부품1.D2, LED2.anode
  N2: 부품1.D3_PWM, LED4.anode
  N3: 부품1.D4, LED5.anode
  N4: R1.Pin_0, R2.Pin_0, R3.Pin_0
  N5: R1.Pin_1, LED5.cathode
  N6: LED2.cathode, R3.Pin_1
  N7: R2.Pin_1, LED4.cathode
