# Fritzing sketch rc_control (saved by Fritzing 0.8.7b)
breadboards: 1

parts:
  부품1 = Arduino Uno (Rev3)
  S1 = Square Pushbutton
  S2 = H-Bridge with L298N
  J1 = Basic Servo
  M1 = DC Motor
  VCC1 = Battery block 9V

nets:
  N1: 부품1.D8, J1.pulse
  N2: 부품1.D11_PWM/MOSI, S2.ENA
  N3: 부품1.D2, S2.IN1
  N4: 부품1.D3_PWM, S2.IN2
  5V: 부품1.5V, S2.5V, J1.vcc
  GND: 부품1.GND, S2.GND, J1.gnd, VCC1.-
  VIN: 부품1.VIN, S1.leg0, S2.12V, VCC1.+
  N5: S2.M1-01, M1.pin_2
  N6: S2.M1-02, M1.pin_1

custom parts:
  H-Bridge with L298N: h-bridge
