# Fritzing sketch rgb (saved by Fritzing 0.8.7b)
breadboards: 1

parts:
  부품1 = Arduino Uno (Rev3)
  LED1 = RGB LED (com. anode, rbg) [package="5 mm [THT]"]
  R1 = Resistor [tolerance=±5% resistance=220 package=THT]

nets:
  N1: 부품1.D9_PWM, LED1.red_cathode
  N2: 부품1.D10_PWM/SS, LED1.green_cathode
  N3: 부품1.D11_PWM/MOSI, LED1.blue_cathode
  N4: LED1.common_anode, R1.Pin_0
