# Fritzing sketch 정선웅 1 차시  (saved by Fritzing 0.8.7b)
breadboards: 1

parts:
  부품1 = Arduino Uno (Rev3)
  LED1 = LED - 5mm [color="Red (633nm)" package="5 mm [THT]"]
  R1 = Resistor [tolerance=±5% resistance=33 package=THT]

nets:
  N1: 부품1.D13/SCK, LED1.anode
  N2: 부품1.GND, LED1.cathode, R1.Pin_1
